# Fritzing sketch Projeto 4 (saved by Fritzing 0.9.2b)
breadboards: 1

parts:
  Componente1 = SRF05 Ultrasonic Rangefinder
  Componente2 = Arduino Leonardo (Rev3b)
  S1 = Pushbutton [package="[SMD]"]

nets:
  VCC: Componente1.VCC, Componente2.5V
  N1: Componente1.Trig, Componente2.D13_PWM
  N2: Componente1.Echo, Componente2.D12/A11
  GND: Componente1.GND, Componente2.GND
  N3: Componente2.D7, S1.Pin_3, S1.Pin_4
  N4: S1.Pin_1, S1.Pin_2
